# Fritzing sketch design (saved by Fritzing 0.8.3b)
circuit board: 1.73466cm x 1.45622cm
circuit board: 3.03666cm x 3.25488cm
circuit board: 2.30474cm x 1.80429cm
circuit board: 3.10436cm x 2.26338cm
circuit board: 6.3688cm x 2.89749cm
circuit board: 2.51547cm x 1.31511cm
circuit board: 2.64717cm x 1.31511cm
breadboards: 1

parts:
  J1 = female pin header, 20 pins [form="♀ (female)"]
  J2 = female pin header, 20 pins [form="♀ (female)"]
  J3 = female pin header, 10 pins [form="♀ (female)"]
  J4 = female pin header, 10 pins [form="♀ (female)"]
  J5 = female pin header, 8 pins [form="♀ (female)"]
  J6 = female pin header, 8 pins [form="♀ (female)"]
  J7 = female pin header, 2 pins [form="♀ (female)"]
  LED1 = LED - 5mm [color="Yellow (595nm)" package="5 mm [THT]"]
  LED2 = LED - 5mm [color="Green (560nm)" package="5 mm [THT]"]
  LED3 = LED - 5mm [color="Green (560nm)" package="5 mm [THT]"]
  R1 = Resistor [tolerance=±5% resistance=330 package=THT]
  C1 = Ceramic Capacitor [capacitance=100nF package="100 mil [THT, multilayer]"]
  C2 = Ceramic Capacitor [capacitance=100nF package="100 mil [THT, multilayer]"]
  J8 = shrouded pin header, 10 pins [form="♂ (shrouded male)"]
  C3 = Ceramic Capacitor [capacitance=100nF package="100 mil [THT, multilayer]"]
  C4 = Ceramic Capacitor [capacitance=100nF package="100 mil [THT, multilayer]"]
  C6 = Ceramic Capacitor [capacitance=100nF package="100 mil [THT, multilayer]"]
  LED4 = LED - 5mm [color="Red (633nm)" package="5 mm [THT]"]
  R2 = Resistor [tolerance=±5% resistance=330 package=THT]
  LED5 = LED - 5mm [color="Orange (620nm)" package="5 mm [THT]"]
  R3 = Resistor [tolerance=±5% resistance=330 package=THT]
  C5 = Ceramic Capacitor [capacitance=100nF package="200 mil [THT, multilayer]"]
  C7 = Ceramic Capacitor [capacitance=100nF package="100 mil [THT, multilayer]"]
  X2 = DB9 Connector [package=db9]
  T1 = LM35 Temperature Sensor [package="TO92 [THT]"]

nets:
  N1: J1.pin1, LED3.anode
  N2: J1.pin2, LED5.anode
  N3: J1.pin9, J8.pin8
  N4: J1.pin10, J2.pin11, J4.pin1, J6.pin8, J7.pin1, C1.1, C2.0, J8.pin9, C4.1, LED4.anode
  N5: J1.pin11, J2.pin10, J4.pin10, J6.pin7, J7.pin2, LED1.cathode, LED2.cathode, R1.Pin_0, C1.0, C2.1, J8.pin6, J8.pin10, C4.0, C6.1, R2.Pin_1, R3.Pin_0, C7.1, X2.5, T1.+Vs
  N6: J1.pin14, J4.pin2
  N7: J1.pin15, J4.pin3
  N8: J1.pin16, J6.pin4
  N9: J1.pin17, J6.pin3
  N10: J1.pin18, J4.pin9
  N11: J2.pin1, T1.GND
  N12: J2.pin8, T1.Vout
  N13: J2.pin14, J8.pin5
  N14: J2.pin15, J8.pin2
  N15: J2.pin16, J8.pin3
  N16: J2.pin17, J8.pin1
  N17: J3.pin6, LED1.anode
  N18: J3.pin8, LED2.anode
  N19: J5.pin3, C6.0
  N20: J5.pin4, C3.0
  N21: J5.pin5, C3.1
  N22: J5.pin6, C5.0
  N23: J5.pin7, C7.0
  N24: J5.pin8, C5.1
  N25: J6.pin5, X2.3
  N26: J6.pin6, X2.2
  N27: LED3.cathode, R1.Pin_1
  N28: LED4.cathode, R2.Pin_0
  N29: LED5.cathode, R3.Pin_1
